// Logisim project Aufgabe13Gruppe12.circ as structural Verilog: 1 circuit, main circuit main
module main (
  input  Input_2,
  input  Input_1
);

  wire transistor_1_out, transistor_2_out;

  Transistor #(.\type ("n")) transistor_1 (.in(1'b0), .out(transistor_1_out), .gate(Input_1));
  Transistor transistor_2 (.in(1'b1), .out(transistor_2_out), .gate(Input_1));
  Transistor transistor_3 (.in(transistor_2_out), .out(transistor_1_out), .gate(Input_2));
  Transistor #(.\type ("n")) transistor_4 (.in(1'b0), .out(transistor_1_out), .gate(Input_2));
  LED Output (.in(transistor_1_out));
endmodule
